// Logisim project 3x8linedecoder.circ as structural Verilog: 1 circuit, main circuit main
module main (
  input  C,
  input  B,
  input  A,
  output out_4,
  output out_5,
  output out_6,
  output out_7,
  output out_8,
  output out_9,
  output out_10,
  output out_11
);

  wire not_1_out;

  not not_1 (not_1_out, C);
  _74139 #(.ShowInternalStructure("true")) u_74139_1 (
    .pin1(not_1_out), .pin2(A), .pin3(B), .pin4(out_8), .pin5(out_9), .pin6(out_10), .pin7(out_11),
    .pin15(C), .pin14(A), .pin13(B), .pin12(out_4), .pin11(out_5), .pin10(out_6), .pin9(out_7));
endmodule
