// Logisim project 4_Bit_Parallel_Adder.circ as structural Verilog: 6 circuits, main circuit main
module main (
  input  A0,
  input  B0,
  input  c0,
  input  A1,
  input  B1,
  input  A2,
  input  B2,
  input  A3,
  input  B3,
  output C4,
  output S3,
  output S2,
  output S1,
  output S0
);

  Four_Bit_Parallel_Adder four_bit_parallel_adder_1 (
    .x0(A0), .y0(B0), .c0(c0), .x1(A1), .y1(B1), .x2(A2), .y2(B2), .x3(A3), .y3(B3), .S0(S0), .S1(S1),
    .s2(S2), .s3(S3), .Cout(C4));
endmodule

module FA0 (
  input  x0,
  input  y0,
  input  c0,
  output s0,
  output Cout
);

  wire and_1_out, and_2_out, xor_1_out;

  xor xor_1 (xor_1_out, x0, y0);
  xor xor_2 (s0, xor_1_out, c0);
  and and_1 (and_1_out, xor_1_out, c0);
  and and_2 (and_2_out, x0, y0);
  or or_1 (Cout, and_1_out, and_2_out);
endmodule

module FA1 (
  input  x1,
  input  y1,
  input  c1,
  output s1,
  output Cout
);

  wire and_1_out, and_2_out, xor_1_out;

  xor xor_1 (xor_1_out, x1, y1);
  xor xor_2 (s1, xor_1_out, c1);
  and and_1 (and_1_out, xor_1_out, c1);
  and and_2 (and_2_out, x1, y1);
  or or_1 (Cout, and_1_out, and_2_out);
endmodule

module FA2 (
  input  x2,
  input  y2,
  input  c2,
  output s2,
  output Cout
);

  wire and_1_out, and_2_out, xor_1_out;

  xor xor_1 (xor_1_out, x2, y2);
  xor xor_2 (s2, xor_1_out, c2);
  and and_1 (and_1_out, xor_1_out, c2);
  and and_2 (and_2_out, x2, y2);
  or or_1 (Cout, and_1_out, and_2_out);
endmodule

module FA3 (
  input  x3,
  input  y3,
  input  c3,
  output s3,
  output Cout
);

  wire and_1_out, and_2_out, xor_1_out;

  xor xor_1 (xor_1_out, x3, y3);
  xor xor_2 (s3, xor_1_out, c3);
  and and_1 (and_1_out, xor_1_out, c3);
  and and_2 (and_2_out, x3, y3);
  or or_1 (Cout, and_1_out, and_2_out);
endmodule

module Four_Bit_Parallel_Adder (
  input  x0,
  input  y0,
  input  c0,
  input  x1,
  input  y1,
  input  x2,
  input  y2,
  input  x3,
  input  y3,
  output S0,
  output S1,
  output s2,
  output s3,
  output Cout
);

  wire fa0_1_cout, fa1_1_cout, fa2_1_cout;

  FA0 fa0_1 (.x0(x0), .y0(y0), .c0(c0), .s0(S0), .Cout(fa0_1_cout));
  FA1 fa1_1 (.x1(x1), .y1(y1), .c1(fa0_1_cout), .s1(S1), .Cout(fa1_1_cout));
  FA2 fa2_1 (.x2(x2), .y2(y2), .c2(fa1_1_cout), .s2(s2), .Cout(fa2_1_cout));
  FA3 fa3_1 (.x3(x3), .y3(y3), .c3(fa2_1_cout), .s3(s3), .Cout(Cout));
endmodule
