// Logisim project 74151MUXCascading.circ as structural Verilog: 1 circuit, main circuit main
module main (
  input  D4,
  input  D6,
  input  D12,
  input  D14,
  input  D,
  input  D5,
  input  D7,
  input  D13,
  input  D15,
  input  C,
  input  B,
  input  D3,
  input  D1,
  input  D11,
  input  D9,
  input  A,
  input  D2,
  input  D0,
  input  D10,
  input  D8,
  output W
);

  wire n74151_1_pin5, n74151_1_pin8, n74151_1_pin16, n74151_2_pin5, n74151_2_pin7, n74151_2_pin8,
       n74151_2_pin16;

  _74151 #(.VccGndPorts("true")) u_74151_1 (
    .pin1(D3), .pin2(D2), .pin3(D1), .pin4(D0), .pin5(n74151_1_pin5), .pin7(D), .pin8(n74151_1_pin8),
    .pin16(n74151_1_pin16), .pin15(D4), .pin14(D5), .pin13(D6), .pin12(D7), .pin11(A), .pin10(B), .pin9(C));  // open: pin6
  _74151 #(.VccGndPorts("true")) u_74151_2 (
    .pin1(D11), .pin2(D10), .pin3(D9), .pin4(D8), .pin5(n74151_2_pin5), .pin7(n74151_2_pin7),
    .pin8(n74151_2_pin8), .pin16(n74151_2_pin16), .pin15(D12), .pin14(D13), .pin13(D14), .pin12(D15),
    .pin11(A), .pin10(B), .pin9(C));  // open: pin6
  not not_1 (n74151_2_pin7, D);
  or or_1 (W, n74151_2_pin5, n74151_1_pin5);
  // also tied to GND on the sheet: {n74151_1_pin8, n74151_2_pin8}
  // also tied to VCC on the sheet: {n74151_1_pin16, n74151_2_pin16}
endmodule
