// Logisim project 74194IC.circ as structural Verilog: 4 circuits, main circuit main
module main (
  input  A,
  input  B,
  input  C,
  input  D,
  input  SR,
  input  SL,
  input  S1,
  input  S0
);

  wire CLK_out, ic74194_1_qa, ic74194_1_qb, ic74194_1_qc, ic74194_1_qd, RST_out;

  Button RST (.out(RST_out));
  Clock CLK (.out(CLK_out));
  IC74194 ic74194_1 (
    .B(B), .A(A), .D(D), .C(C), .Shift_Right(SR), .Shift_Left(SL), .S1(S1), .S0(S0), .CLK(CLK_out),
    .RST(RST_out), .QA(ic74194_1_qa), .QD(ic74194_1_qd), .QC(ic74194_1_qc), .QB(ic74194_1_qb));
  LED QD (.in(ic74194_1_qd));
  LED QC (.in(ic74194_1_qc));
  LED QB (.in(ic74194_1_qb));
  LED QA (.in(ic74194_1_qa));
endmodule

module MUX4TO1 (
  input  I0,
  input  I1,
  input  I2,
  input  I3,
  input  S0,
  input  S1,
  output X
);

  wire multiplexer_1_out, multiplexer_2_out;

  Multiplexer multiplexer_1 (.in0(I0), .in1(I2), .out(multiplexer_1_out), .sel(S0));
  Multiplexer multiplexer_2 (.in0(I1), .in1(I3), .out(multiplexer_2_out), .sel(S0));
  Multiplexer multiplexer_3 (.in0(multiplexer_1_out), .in1(multiplexer_2_out), .out(X), .sel(S1));
endmodule

module IC74194 (
  input  B,
  input  A,
  input  D,
  input  C,
  input  Shift_Right,
  input  Shift_Left,
  input  S1,
  input  S0,
  input  CLK,
  input  RST,
  output QA,
  output QD,
  output QC,
  output QB
);

  wire MUX0_x, MUX1_x, MUX2_x, MUX3_x, undriven;

  MUX4TO1 MUX3 (.I0(QD), .I1(QC), .I2(Shift_Right), .I3(D), .S0(S0), .S1(S1), .X(MUX3_x));
  D_Flip_Flop Q3 (.D(MUX3_x), .clk(CLK), .Q(QD), .preset(undriven), .reset(RST));  // open: Qn
  MUX4TO1 MUX2 (.I0(QC), .I1(QB), .I2(QD), .I3(C), .S0(S0), .S1(S1), .X(MUX2_x));
  D_Flip_Flop Q2 (.D(MUX2_x), .clk(CLK), .Q(QC), .reset(RST));  // open: Qn, preset
  MUX4TO1 MUX1 (.I0(QB), .I1(QA), .I2(QC), .I3(B), .S0(S0), .S1(S1), .X(MUX1_x));
  D_Flip_Flop Q1 (.D(MUX1_x), .clk(CLK), .Q(QB), .reset(RST));  // open: Qn, preset
  MUX4TO1 MUX0 (.I0(QA), .I1(Shift_Left), .I2(QB), .I3(A), .S0(S0), .S1(S1), .X(MUX0_x));
  D_Flip_Flop Q0 (.D(MUX0_x), .clk(CLK), .Q(QA), .reset(RST));  // open: Qn, preset
endmodule

module Lab10_last (
  input  A,
  input  B,
  input  C,
  input  D,
  input  SR,
  input  SL
);

  wire CLK_out, ic74194_1_qa, ic74194_1_qb, ic74194_1_qc, ic74194_1_qd, RST_out;

  Button RST (.out(RST_out));
  Clock CLK (.out(CLK_out));
  IC74194 ic74194_1 (
    .B(B), .A(A), .D(D), .C(C), .Shift_Right(ic74194_1_qa), .Shift_Left(SL), .S1(1'b0), .S0(1'b1),
    .CLK(CLK_out), .RST(RST_out), .QA(ic74194_1_qa), .QD(ic74194_1_qd), .QC(ic74194_1_qc), .QB(ic74194_1_qb));
  LED QD (.in(ic74194_1_qd));
  LED QC (.in(ic74194_1_qc));
  LED QB (.in(ic74194_1_qb));
  LED QA (.in(ic74194_1_qa));
endmodule
