// Logisim project CEP.circ as structural Verilog: 1 circuit, main circuit main
module main (
  input  X
);

  wire and_1_out, and_2_out, CLK_out, not_1_out, not_2_out, not_3_out, not_4_out, or_1_out, Q0_q, Q1_q, Q2_q;

  Clock CLK (.out(CLK_out));
  D_Flip_Flop Q0 (.D(X), .clk(CLK_out), .Q(Q0_q));  // open: Qn, preset, reset
  LED L0 (.in(Q0_q));
  LED L1 (.in(Q1_q));
  D_Flip_Flop Q1 (.D(Q0_q), .clk(CLK_out), .Q(Q1_q));  // open: Qn, preset, reset
  not not_1 (not_1_out, Q2_q);
  not not_2 (not_2_out, Q1_q);
  not not_3 (not_3_out, Q0_q);
  not not_4 (not_4_out, Q0_q);
  D_Flip_Flop Q2 (.D(Q1_q), .clk(CLK_out), .Q(Q2_q));  // open: Qn, preset, reset
  and and_1 (and_1_out, not_1_out, not_2_out, not_3_out);
  and and_2 (and_2_out, Q2_q, Q1_q, not_4_out);
  LED L2 (.in(Q2_q));
  or or_1 (or_1_out, and_1_out, and_2_out);
  LED led_1 (.in(or_1_out));
endmodule
