// Logisim project CEP_2.circ as structural Verilog: 1 circuit, main circuit main
module main (
  input  X
);

  wire and_1_out, and_2_out, and_3_out, and_4_out, and_5_out, and_6_out, and_7_out, and_8_out, and_9_out,
       and_10_out, and_11_out, Clk_out, not_1_out, not_2_out, not_3_out, not_4_out, or_1_out, or_2_out,
       or_3_out, or_4_out, Q0_q, Q1_q, Q2_q;

  not not_1 (not_1_out, X);
  and and_1 (and_1_out, not_3_out, Q2_q, not_1_out);
  and and_2 (and_2_out, not_3_out, not_2_out, not_1_out);
  and and_3 (and_3_out, Q0_q, Q1_q, not_4_out, not_1_out);
  and and_4 (and_4_out, not_4_out, not_2_out, Q1_q, X);
  and and_5 (and_5_out, Q0_q, not_3_out, not_1_out);
  and and_6 (and_6_out, Q1_q, not_2_out, not_4_out);
  or or_1 (or_1_out, and_1_out, and_2_out, and_3_out, and_4_out);
  or or_2 (or_2_out, and_5_out, and_6_out);
  not not_2 (not_2_out, Q0_q);
  D_Flip_Flop Q0 (.D(or_1_out), .clk(Clk_out), .Q(Q0_q));  // open: Qn, preset, reset
  Clock Clk (.out(Clk_out));
  not not_3 (not_3_out, Q1_q);
  D_Flip_Flop Q1 (.D(or_2_out), .clk(Clk_out), .Q(Q1_q));  // open: Qn, preset, reset
  and and_7 (and_7_out, not_3_out, Q1_q, Q0_q);
  and and_8 (and_8_out, X, Q1_q, not_2_out);
  D_Flip_Flop Q2 (.D(or_4_out), .clk(Clk_out), .Q(Q2_q));  // open: Qn, preset, reset
  or or_3 (or_3_out, and_7_out, and_8_out);
  not not_4 (not_4_out, Q2_q);
  LED Y (.in(or_3_out));
  and and_9 (and_9_out, X, Q0_q, not_3_out);
  and and_10 (and_10_out, Q0_q, Q1_q, not_4_out, not_1_out);
  and and_11 (and_11_out, Q2_q, not_2_out, not_3_out, not_1_out);
  or or_4 (or_4_out, and_9_out, and_10_out, and_11_out);
endmodule
