// Logisim project CEP_3.circ as structural Verilog: 6 circuits, main circuit main
module main (
);

  FSM_main fsm_main_1 ();  // open: X, Clk, RESET, Y
endmodule

module D2_Logic (
  input  Q2,
  input  Q1,
  input  Q0,
  input  X,
  output D2
);

  wire and_1_out, and_2_out, not_1_out, not_2_out, not_3_out, not_4_out;

  not not_1 (not_1_out, Q2);
  not not_2 (not_2_out, Q1);
  not not_3 (not_3_out, Q0);
  not not_4 (not_4_out, X);
  and and_1 (and_1_out, not_1_out, not_3_out, X);
  and and_2 (and_2_out, not_2_out, Q0, not_4_out);
  or or_1 (D2, and_1_out, and_2_out);
endmodule

module D1_Logic (
  input  Q2,
  input  Q1,
  input  Q0,
  input  X,
  output D1
);

  wire and_1_out, and_2_out, not_1_out, not_2_out, not_3_out, not_4_out;

  not not_1 (not_1_out, Q2);
  not not_2 (not_2_out, Q1);
  not not_3 (not_3_out, Q0);
  not not_4 (not_4_out, X);
  and and_1 (and_1_out, not_1_out, not_2_out, not_4_out);
  and and_2 (and_2_out, not_1_out, not_3_out, not_4_out);
  or or_1 (D1, and_1_out, and_2_out);
endmodule

module D0_Logic (
  input  Q2,
  input  Q1,
  input  Q0,
  input  X,
  output D0
);

  wire and_1_out, and_2_out, not_1_out, not_2_out, not_4_out;

  not not_1 (not_1_out, Q2);
  not not_2 (not_2_out, Q1);
  // NOT_Gate not_3 has open pins: in=Q0, out=open
  not not_4 (not_4_out, X);
  and and_1 (and_1_out, not_1_out, not_2_out, not_4_out);
  and and_2 (and_2_out, not_1_out, Q1, not_4_out);
  or or_1 (D0, and_1_out, and_2_out);
endmodule

module Y_Logic (
  input  Q2,
  input  Q1,
  input  Q0,
  input  X,
  output Y
);

  wire and_1_out, and_2_out, not_1_out, not_2_out, not_3_out, not_4_out;

  not not_1 (not_1_out, Q2);
  not not_2 (not_2_out, Q1);
  not not_3 (not_3_out, Q0);
  not not_4 (not_4_out, X);
  and and_1 (and_1_out, not_1_out, Q1, not_3_out, X);
  and and_2 (and_2_out, Q2, not_2_out, not_3_out, not_4_out);
  or or_1 (Y, and_1_out, and_2_out);
endmodule

module FSM_main (
  input  X,
  input  Clk,
  input  RESET,
  output Y
);

  wire d0_logic_1_d0, d1_logic_1_d1, d2_logic_1_d2, Q0_q, Q1_q, Q2_q;

  D_Flip_Flop Q2 (.D(d2_logic_1_d2), .clk(Clk), .Q(Q2_q), .reset(RESET));  // open: Qn, preset
  D2_Logic d2_logic_1 (.Q2(Q2_q), .Q1(Q1_q), .Q0(Q0_q), .X(X), .D2(d2_logic_1_d2));
  D_Flip_Flop Q1 (.D(d1_logic_1_d1), .clk(Clk), .Q(Q1_q), .reset(RESET));  // open: Qn, preset
  D1_Logic d1_logic_1 (.Q2(Q2_q), .Q1(Q1_q), .Q0(Q0_q), .X(X), .D1(d1_logic_1_d1));
  D_Flip_Flop Q0 (.D(d0_logic_1_d0), .clk(Clk), .Q(Q0_q), .reset(RESET));  // open: Qn, preset
  D0_Logic d0_logic_1 (.Q2(Q2_q), .Q1(Q1_q), .Q0(Q0_q), .X(X), .D0(d0_logic_1_d0));
  Y_Logic y_logic_1 (.Q2(Q2_q), .Q1(Q1_q), .Q0(Q0_q), .X(X), .Y(Y));
endmodule
