// Logisim project CEP_GPT.circ as structural Verilog: 1 circuit, main circuit main
module main (
  input  X,
  input  RESET
);

  wire and_1_out, and_2_out, and_3_out, and_4_out, and_5_out, and_6_out, CLK_out, not_1_out, not_2_out,
       not_3_out, not_4_out, not_5_out, not_6_out, not_7_out, not_8_out, or_1_out, or_2_out, or_3_out, Q0_q,
       Q1_q;

  Clock CLK (.out(CLK_out));
  not not_1 (not_1_out, Q1_q);
  not not_2 (not_2_out, X);
  and and_1 (and_1_out, not_1_out, Q0_q);
  and and_2 (and_2_out, Q1_q, not_2_out);
  or or_1 (or_1_out, and_1_out, and_2_out);
  D_Flip_Flop Q1 (.D(or_1_out), .clk(CLK_out), .Q(Q1_q), .reset(RESET));  // open: Qn, preset
  not not_3 (not_3_out, Q1_q);
  not not_4 (not_4_out, Q0_q);
  not not_5 (not_5_out, X);
  not not_6 (not_6_out, Q1_q);
  and and_3 (and_3_out, not_3_out, not_4_out, not_5_out);
  and and_4 (and_4_out, not_6_out, Q0_q, X);
  D_Flip_Flop Q0 (.D(or_2_out), .clk(CLK_out), .Q(Q0_q), .reset(RESET));  // open: Qn, preset
  LED led_1 (.in(Q1_q));
  or or_2 (or_2_out, and_3_out, and_4_out);
  LED led_2 (.in(Q0_q));
  not not_7 (not_7_out, Q0_q);
  not not_8 (not_8_out, X);
  and and_5 (and_5_out, Q1_q, not_7_out, X);
  and and_6 (and_6_out, Q1_q, Q0_q, not_8_out);
  or or_3 (or_3_out, and_5_out, and_6_out);
  LED Z (.in(or_3_out));
endmodule
