// Logisim project LAB12.circ as structural Verilog: 1 circuit, main circuit main
module main (
  input  X
);

  wire and_1_out, and_2_out, CLK_out, D0_q, D1_q, not_1_out, not_2_out, or_1_out, RESET_out;

  Button RESET (.out(RESET_out));
  Clock CLK (.out(CLK_out));
  or or_1 (or_1_out, D1_q, D0_q);
  not not_1 (not_1_out, D1_q);
  and and_1 (and_1_out, or_1_out, X);
  and and_2 (and_2_out, not_1_out, X);
  D_Flip_Flop D1 (.D(and_1_out), .clk(CLK_out), .Q(D1_q), .reset(RESET_out));  // open: Qn, preset
  D_Flip_Flop D0 (.D(and_2_out), .clk(CLK_out), .Q(D0_q), .reset(RESET_out));  // open: Qn, preset
  not not_2 (not_2_out, X);
  LED Z (.in(not_2_out));
endmodule
