// Logisim project Lab3_1a.circ as structural Verilog: 1 circuit, main circuit main
module main (
  input  X,
  input  Y,
  output Difference,
  output Borrow
);

  wire not_1_out;

  not not_1 (not_1_out, X);
  xor xor_1 (Difference, X, Y);
  and and_1 (Borrow, not_1_out, Y);
endmodule
