// Logisim project Lab3_1aFull.circ as structural Verilog: 1 circuit, main circuit main
module main (
  input  X,
  input  Y,
  input  Bout,
  output Difference,
  output Bin
);

  wire and_1_out, and_2_out, not_1_out, not_2_out, XY_out;

  xor XY (XY_out, X, Y);
  not not_1 (not_1_out, X);
  not not_2 (not_2_out, XY_out);
  xor xor_1 (Difference, XY_out, Bout);
  and and_1 (and_1_out, not_2_out, Bout);
  and and_2 (and_2_out, not_1_out, Y);
  or or_1 (Bin, and_1_out, and_2_out);
endmodule
