// Logisim project Lab5FullAdder.circ as structural Verilog: 1 circuit, main circuit main
module main (
  input  A,
  input  B,
  input  C,
  output Carry,
  output Sum
);

  wire n74138_1_pin4, n74138_1_pin6, n74138_1_pin7, n74138_1_pin9, n74138_1_pin10, n74138_1_pin11,
       n74138_1_pin12, n74138_1_pin13, n74138_1_pin14, not_1_out, not_2_out, not_3_out, not_4_out, not_5_out,
       not_6_out, not_7_out;

  _74138 #(.ShowInternalStructure("true")) u_74138_1 (
    .pin1(A), .pin2(B), .pin3(C), .pin4(n74138_1_pin4), .pin5(n74138_1_pin4), .pin6(n74138_1_pin6),
    .pin7(n74138_1_pin7), .pin14(n74138_1_pin14), .pin13(n74138_1_pin13), .pin12(n74138_1_pin12),
    .pin11(n74138_1_pin11), .pin10(n74138_1_pin10), .pin9(n74138_1_pin9));  // open: pin15
  not not_1 (not_1_out, n74138_1_pin12);
  not not_2 (not_2_out, n74138_1_pin10);
  not not_3 (not_3_out, n74138_1_pin9);
  not not_4 (not_4_out, n74138_1_pin14);
  not not_5 (not_5_out, n74138_1_pin13);
  not not_6 (not_6_out, n74138_1_pin11);
  not not_7 (not_7_out, n74138_1_pin7);
  or or_1 (Carry, not_7_out, not_1_out, not_2_out, not_3_out);
  or or_2 (Sum, not_4_out, not_5_out, not_6_out, not_7_out);
  // also tied to GND on the sheet: n74138_1_pin4
  // also tied to VCC on the sheet: n74138_1_pin6
endmodule
