// Logisim project NAND_Equivalent_Full_Subtractor.circ as structural Verilog: 1 circuit, main circuit main
module main (
  input  X,
  input  Y,
  input  Bout,
  output Difference,
  output Bin
);

  wire nand_1_out, nand_2_out, nand_3_out, nand_4_out, nand_5_out, nand_6_out, nand_7_out, nand_8_out,
       nand_9_out, nand_10_out, nand_11_out, nand_12_out, nand_13_out;

  nand nand_1 (nand_1_out, X, X);
  nand nand_2 (nand_2_out, Y, Y);
  nand nand_3 (nand_3_out, X, X);
  nand nand_4 (nand_4_out, nand_1_out, Y);
  nand nand_5 (nand_5_out, X, nand_2_out);
  nand nand_6 (nand_6_out, nand_3_out, Y);
  nand nand_7 (nand_7_out, nand_4_out, nand_5_out);
  nand nand_8 (nand_8_out, nand_7_out, nand_7_out);
  nand nand_9 (nand_9_out, Bout, Bout);
  nand nand_10 (nand_10_out, nand_7_out, nand_7_out);
  nand nand_11 (nand_11_out, nand_8_out, Bout);
  nand nand_12 (nand_12_out, nand_7_out, nand_9_out);
  nand nand_13 (nand_13_out, nand_10_out, Bout);
  nand nand_14 (Difference, nand_11_out, nand_12_out);
  nand nand_15 (Bin, nand_13_out, nand_6_out);

  // Notes on the sheet:
  //   X⊕Y⊕Bout
  //   Bout(X⊕Y)' + X'Y
endmodule
