// Logisim project NEW_CEP.circ as structural Verilog: 9 circuits, main circuit main
module main (
  input  X
);

  wire CLK_out, fsm_main_ic_1_q0_out, fsm_main_ic_1_q1_out, fsm_main_ic_1_q2_out, fsm_main_ic_1_y, not_1_out,
       RST_FSM_out, RST_SR_out, s_r_ff_1_q, s_r_ff_1_qn, seven_segment_display_1_a,
       seven_segment_display_1_b, seven_segment_display_1_c, seven_segment_display_1_d,
       seven_segment_display_1_e, seven_segment_display_1_f, seven_segment_display_1_g;

  Clock CLK (.out(CLK_out));
  Button RST_FSM (.out(RST_FSM_out));
  Button RST_SR (.out(RST_SR_out));
  S_R_Flip_Flop s_r_ff_1 (
    .S(s_r_ff_1_qn), .R(s_r_ff_1_q), .clk(not_1_out), .Q(s_r_ff_1_q), .reset(RST_SR_out), .Qn(s_r_ff_1_qn));  // open: preset
  not not_1 (not_1_out, s_r_ff_1_q);
  FSM_main_IC fsm_main_ic_1 (
    .X(X), .CLK(CLK_out), .RESET(RST_FSM_out), .Y(fsm_main_ic_1_y), .Q2_out(fsm_main_ic_1_q2_out),
    .Q1_out(fsm_main_ic_1_q1_out), .Q0_out(fsm_main_ic_1_q0_out));
  Seven_Segment_Display seven_segment_display_1 (
    .Q2(fsm_main_ic_1_q2_out), .Q1(fsm_main_ic_1_q1_out), .Q0(fsm_main_ic_1_q0_out),
    .a(seven_segment_display_1_a), .b(seven_segment_display_1_b), .c(seven_segment_display_1_c),
    .d(seven_segment_display_1_d), .e(seven_segment_display_1_e), .f(seven_segment_display_1_f),
    .g(seven_segment_display_1_g));
  LED Y (.in(fsm_main_ic_1_y));
  _7_Segment_Display State (
    .g(seven_segment_display_1_g), .f(seven_segment_display_1_f), .a(seven_segment_display_1_a),
    .b(seven_segment_display_1_b), .e(seven_segment_display_1_e), .d(seven_segment_display_1_d),
    .c(seven_segment_display_1_c));  // open: dp
endmodule

module D2_Logic (
  input  X,
  input  Q2,
  input  Q1,
  input  Q0,
  output D2
);

  wire and_1_out, and_2_out, and_3_out, not_1_out, not_2_out, not_3_out, not_4_out;

  not not_1 (not_1_out, X);
  not not_2 (not_2_out, Q0);
  not not_3 (not_3_out, X);
  not not_4 (not_4_out, Q1);
  and and_1 (and_1_out, not_1_out, Q2, not_2_out);
  and and_2 (and_2_out, not_3_out, Q1, Q0);
  and and_3 (and_3_out, X, not_4_out, Q0);
  or or_1 (D2, and_1_out, and_2_out, and_3_out);
endmodule

module D1_Logic (
  input  X,
  input  Q2,
  input  Q1,
  input  Q0,
  output D1
);

  wire and_1_out, and_2_out, not_1_out, not_2_out, not_3_out;

  not not_1 (not_1_out, X);
  not not_2 (not_2_out, Q1);
  not not_3 (not_3_out, Q0);
  and and_1 (and_1_out, not_1_out, not_2_out, Q0);
  and and_2 (and_2_out, Q1, not_3_out);
  or or_1 (D1, and_1_out, and_2_out);
endmodule

module D0_logic (
  input  X,
  input  Q2,
  input  Q1,
  input  Q0,
  output D0
);

  wire and_1_out, and_2_out, and_3_out, not_1_out, not_2_out, not_3_out, not_4_out, not_5_out;

  not not_1 (not_1_out, X);
  not not_2 (not_2_out, Q1);
  not not_3 (not_3_out, Q0);
  not not_4 (not_4_out, X);
  not not_5 (not_5_out, Q0);
  and and_1 (and_1_out, not_1_out, not_2_out, not_3_out);
  and and_2 (and_2_out, not_4_out, Q1, Q0);
  and and_3 (and_3_out, X, Q1, not_5_out);
  or or_1 (D0, and_1_out, and_2_out, and_3_out);
endmodule

module Y_Logic (
  input  X,
  input  Q2,
  input  Q1,
  input  Q0,
  output Y
);

  wire and_1_out, and_2_out, and_3_out, not_1_out, not_2_out, not_3_out, not_4_out;

  not not_1 (not_1_out, X);
  not not_2 (not_2_out, Q0);
  not not_3 (not_3_out, X);
  not not_4 (not_4_out, Q0);
  and and_1 (and_1_out, not_1_out, Q2, not_2_out);
  and and_2 (and_2_out, not_3_out, Q1, Q0);
  and and_3 (and_3_out, X, Q1, not_4_out);
  or or_1 (Y, and_1_out, and_2_out, and_3_out);
endmodule

module FSM_main (
  input  X,
  input  FSM_CLK,
  input  FSM_RESET,
  output Y_out,
  output Q2_out,
  output Q1_out,
  output Q0_out
);

  wire d0_logic_1_d0, d1_logic_1_d1, d2_logic_1_d2;

  _7474 #(.ShowInternalStructure("true")) Q2_and_Q1 ();  // open: pin1, pin2, pin3, pin4, pin5, pin6, pin13, pin12, pin11, pin10, pin9, pin8
  D2_Logic d2_logic_1 (.X(X), .Q2(Q2_out), .Q1(Q1_out), .Q0(Q0_out), .D2(d2_logic_1_d2));
  D_Flip_Flop Q2 (.D(d2_logic_1_d2), .clk(FSM_CLK), .Q(Q2_out), .reset(FSM_RESET));  // open: Qn, preset
  _7474 #(.ShowInternalStructure("true")) Q0_IC ();  // open: pin1, pin2, pin3, pin4, pin5, pin6, pin13, pin12, pin11, pin10, pin9, pin8
  D_Flip_Flop Q1 (.D(d1_logic_1_d1), .clk(FSM_CLK), .Q(Q1_out), .reset(FSM_RESET));  // open: Qn, preset
  D1_Logic d1_logic_1 (.X(X), .Q2(Q2_out), .Q1(Q1_out), .Q0(Q0_out), .D1(d1_logic_1_d1));
  D0_logic d0_logic_1 (.X(X), .Q2(Q2_out), .Q1(Q1_out), .Q0(Q0_out), .D0(d0_logic_1_d0));
  D_Flip_Flop Q0 (.D(d0_logic_1_d0), .clk(FSM_CLK), .Q(Q0_out), .reset(FSM_RESET));  // open: Qn, preset
  Y_Logic y_logic_1 (.X(X), .Q2(Q2_out), .Q1(Q1_out), .Q0(Q0_out), .Y(Y_out));
endmodule

module Seven_Segment_Display (
  input  Q2,
  input  Q1,
  input  Q0,
  output a,
  output b,
  output c,
  output d,
  output e,
  output f,
  output g
);

  wire n7447_1_pin3, n7447_1_pin6, n7447_1_pin9, n7447_1_pin10, n7447_1_pin11, n7447_1_pin12, n7447_1_pin13,
       n7447_1_pin14, n7447_1_pin15;

  _7447 #(.ShowInternalStructure("true")) u_7447_1 (
    .pin1(Q1), .pin2(Q2), .pin3(n7447_1_pin3), .pin4(n7447_1_pin3), .pin5(n7447_1_pin3), .pin6(n7447_1_pin6),
    .pin7(Q0), .pin15(n7447_1_pin15), .pin14(n7447_1_pin14), .pin13(n7447_1_pin13), .pin12(n7447_1_pin12),
    .pin11(n7447_1_pin11), .pin10(n7447_1_pin10), .pin9(n7447_1_pin9));
  not not_1 (a, n7447_1_pin13);
  not not_2 (b, n7447_1_pin12);
  not not_3 (c, n7447_1_pin11);
  not not_4 (d, n7447_1_pin10);
  not not_5 (e, n7447_1_pin9);
  not not_6 (f, n7447_1_pin15);
  not not_7 (g, n7447_1_pin14);
  // also tied to GND on the sheet: n7447_1_pin6
  // also tied to VCC on the sheet: n7447_1_pin3
endmodule

module FSM_main_IC (
  input  X,
  input  CLK,
  input  RESET,
  output Y,
  output Q2_out,
  output Q1_out,
  output Q0_out
);

  wire d0_logic_1_d0, d2_logic_1_d2, not_1_out, Q2_and_Q1_pin12;

  not not_1 (not_1_out, RESET);
  D2_Logic d2_logic_1 (.X(X), .Q2(Q2_out), .Q1(Q1_out), .Q0(Q0_out), .D2(d2_logic_1_d2));
  _7474 Q2_and_Q1 (
    .pin1(not_1_out), .pin2(d2_logic_1_d2), .pin3(CLK), .pin5(Q2_out), .pin13(not_1_out),
    .pin12(Q2_and_Q1_pin12), .pin11(CLK), .pin9(Q1_out));  // open: pin4, pin6, pin10, pin8
  D1_Logic d1_logic_1 (.X(X), .Q2(Q2_out), .Q1(Q1_out), .Q0(Q0_out), .D1(Q2_and_Q1_pin12));
  D0_logic d0_logic_1 (.X(X), .Q2(Q2_out), .Q1(Q1_out), .Q0(Q0_out), .D0(d0_logic_1_d0));
  _7474 Q0 (
    .pin1(not_1_out), .pin2(d0_logic_1_d0), .pin3(CLK), .pin5(Q0_out));  // open: pin4, pin6, pin13, pin12, pin11, pin10, pin9, pin8
  Y_Logic y_logic_1 (.X(X), .Q2(Q2_out), .Q1(Q1_out), .Q0(Q0_out), .Y(Y));
endmodule

module Timer (
);

  wire comparator_1_eq, not_1_out, not_2_out, not_3_out, or_1_out, RESET_out, s_r_ff_1_q, Start_out;
  wire [3:0] counter_1_q;

  not not_1 (not_1_out, not_3_out);
  not not_2 (not_2_out, not_1_out);
  not not_3 (not_3_out, not_2_out);
  Counter #(.max('hf), .width(4)) counter_1 (
    .clr(or_1_out), .load(1'b0), .up(1'b1), .count(s_r_ff_1_q), .clk(not_2_out), .Q(counter_1_q));  // open: D, carry
  Button RESET (.out(RESET_out));
  Button Start (.out(Start_out));
  or or_1 (or_1_out, comparator_1_eq, RESET_out);
  S_R_Flip_Flop s_r_ff_1 (.S(Start_out), .R(or_1_out), .Q(s_r_ff_1_q));  // open: clk, reset, Qn, preset
  Comparator #(.width(4)) comparator_1 (.a(counter_1_q), .b(4'b1010), .eq(comparator_1_eq));  // open: gt, lt
  LED led_1 (.in(comparator_1_eq));
endmodule
